# Fritzing sketch relayUnit (saved by Fritzing 0.9.3b)
breadboards: 1

parts:
  LED1 = smd LED [color="Green (555nm)" package="0805 [SMD]"]
  LM1 = RioRand LM2596
  U4 = 2-Channel 5v Relay Shield [package=relay-2ch5v10a]
  J2 = Screw terminal - 2 pins [package=THT]
  J3 = Screw terminal - 2 pins [package=THT]
  J4 = Screw terminal - 2 pins [package=THT]
  J1 = Screw terminal - 2 pins [package=THT]
  U3 = NodeMCU V1.0
  R1 = Resistor [tolerance=±5% resistance=220 package="0603 [SMD]"]
  R4 = Resistor [tolerance=±5% resistance=220 package="1206 [SMD]"]
  R5 = Resistor [tolerance=±5% resistance=220 package="1206 [SMD]"]
  JACK1 = 2.1mm DC Barrel Jack
  VALVE1 = Plastic Solenoid Valve

nets:
  N1: LED1.cathode, R1.Pin_1
  GND: LED1.anode, LM1.Pin_3, U4.GND, J2.pin2, J3.pin2, J4.pin2, J1.pin2, U3.GND
  N2: LM1.Pin_0, U4.K1-In, JACK1.center
  N3: LM1.Pin_1, JACK1.sleeve, VALVE1.no_name_yet#1
  N4: LM1.Pin_2, J2.pin1, U3.Vin
  VCC: U4.VCC, J1.pin1, U3.3V3, R4.Pin_0, R5.Pin_0
  N5: U4.IN1, U3.D7
  N6: U4.K1-On, VALVE1.no_name_yet#2
  N7: J3.pin1, U3.D5, R5.Pin_1
  N8: J4.pin1, U3.D6, R4.Pin_1
  N9: U3.D0, R1.Pin_0

notes:
  12-24VDC Power supply depending on your Solenoid Valve
  These two screw terminals are for the inclusion of a level switch or manual button to activate the valve if desired

custom parts:
  2-Channel 5v Relay Shield: 2 Channel 5v Relay Shield w. 2x SPD-06VDC-SD-C
  NodeMCU V1.0: ESP8266 based NodeMCU
  2.1mm DC Barrel Jack: 2.1mm DC Barrel Jack with Thru-Hole Connectors (breadboardable)
